# Fritzing sketch Finisher (saved by Fritzing 0.9.3b)
breadboards: 2

parts:
  Raspberry_Pi_Zero1 = Raspberry Pi Zero
  IC1 = MCP3008 8-channel 10-bit ADC [part_number=MCP3008]
  R2 = Resistor [tolerance=±5% resistance=10k package="0402 [SMD]"]
  R3 = Resistor [tolerance=±5% resistance=6.8k package="0402 [SMD]"]
  R8 = Resistor [tolerance=±5% resistance=6.8k package="0402 [SMD]"]
  R9 = Resistor [tolerance=±5% resistance=10k package="0402 [SMD]"]
  Part4 = Adafruit PowerBoost 1000C [part_number="Adafruit #2465"]
  S1 = Pushbutton [package="[THT]"]
  D1 = Rectifier Diode [part_number=1N4001 package="300 mil [THT]"]
  D2 = Rectifier Diode [part_number=1N4001 package="300 mil [THT]"]
  D3 = Rectifier Diode [part_number=1N4001 package="300 mil [THT]"]
  R10 = Resistor [tolerance=±5% resistance=10k package="0402 [SMD]"]
  R11 = Resistor [tolerance=±5% resistance=100k package="0402 [SMD]"]
  R12 = Resistor [tolerance=±5% resistance=10k package="0402 [SMD]"]
  Part6 = Arduino Uno (Rev3)
  Part7 = LIDAR-Lite
  R13 = Resistor [tolerance=±5% resistance=220 package=THT]
  Part8 = Adafruit RFM9x LoRa Radio [part_number="Adafruit #3072 and #3073"]
  LED3 = LED - 5mm [color="Yellow (595nm)" package="5 mm [THT]"]
  LED4 = LED - 5mm [color="Blue (525nm)" package="5 mm [THT]"]
  Part9 = TXB0104 4-channel Bi-Directional Level Shifter
  R14 = Resistor [tolerance=±5% resistance=220 package=THT]
  R15 = Resistor [tolerance=±5% resistance=220 package=THT]
  BAT1 = Battery Holders [package=lipo-1100mAh]  # not connected
  LED5 = LED - 5mm [color="Red (633nm)" package="5 mm [THT]"]
  R16 = Resistor [tolerance=±5% resistance=220 package=THT]

nets:
  N1: Raspberry_Pi_Zero1.3v3, IC1.no_name_yet#9, IC1.no_name_yet#10, Part9.LV
  N2: Raspberry_Pi_Zero1.GPIO2, Part6.A4/SDA
  N3: Raspberry_Pi_Zero1.GPIO3, Part6.A5/SCL
  GND: Raspberry_Pi_Zero1.GND, Raspberry_Pi_Zero1.GIPO17, Raspberry_Pi_Zero1.GIPO22, Raspberry_Pi_Zero1.GIPO11, Raspberry_Pi_Zero1.GIPO5, Raspberry_Pi_Zero1.GIPO26, Raspberry_Pi_Zero1.GIPO12, Raspberry_Pi_Zero1.GIPO24, Raspberry_Pi_Zero1.GIPO18, IC1.no_name_yet#11, IC1.no_name_yet#12, IC1.no_name_yet#14, IC1.no_name_yet#16, R2.Pin_0, R9.Pin_0, Part4.GND, R10.Pin_0, R11.Pin_0, R12.Pin_0, Part6.GND, Part7.GND, Part8.GND, LED3.cathode, LED4.cathode, Part9.GND, Part9.OE, LED5.cathode
  N4: Raspberry_Pi_Zero1.GIPO27, Raspberry_Pi_Zero1.GIPO23, IC1.no_name_yet#13
  N5: Raspberry_Pi_Zero1.GIPO13, Raspberry_Pi_Zero1.GIPO19, IC1.no_name_yet#15
  N6: Raspberry_Pi_Zero1.GIPO8, Raspberry_Pi_Zero1.GIPO25
  N7: Raspberry_Pi_Zero1.GIPO15, Part9.A2
  N8: Raspberry_Pi_Zero1.GIPO14, Part9.A3
  5V: Raspberry_Pi_Zero1.5V, Part4.5.0V, Part6.5V, Part7.5V, Part8.VIN, Part9.HV
  N9: IC1.no_name_yet#7, R8.Pin_0, R9.Pin_1
  N10: IC1.no_name_yet#8, R2.Pin_1, R3.Pin_0
  N11: R3.Pin_1, Part4.VLIPO, S1.Pin_1, S1.Pin_2
  N12: R8.Pin_1, Part4.VBUS
  N13: Part4.ENABLE, D1.cathode, R11.Pin_1, R12.Pin_1
  N14: S1.Pin_3, S1.Pin_4, D1.anode, D2.anode
  N15: D2.cathode, D3.anode
  N16: D3.cathode, R10.Pin_1
  N17: Part6.D8, LED4.anode, R15.Pin_0, R15.Pin_1
  N18: Part6.D9_PWM, LED5.anode, R16.Pin_0, R16.Pin_1
  N19: Part6.D11_PWM/MOSI, Part8.MOSI
  N20: Part6.D12/MISO, Part8.MISO
  N21: Part6.D13/SCK, Part8.SCK
  N22: Part6.D0/RX, Part9.B3
  N23: Part6.D1/TX, Part9.B2
  N24: Part6.D2, Part8.RST
  N25: Part6.D3_PWM, Part8.DIO0
  N26: Part6.D4, Part8.CS
  N27: Part6.D5_PWM, Part7.MODE, R13.Pin_0
  N28: Part6.D6_PWM, R13.Pin_1
  N29: Part6.D7, LED3.anode, R14.Pin_0, R14.Pin_1

custom parts:
  Adafruit PowerBoost 1000C: PowerBoost 1000C is the perfect power supply for your portable project! With a built-in load-sharing battery charger circuit, you'll be able to keep your power-hungry project running even while recharging the battery! This little DC/DC boost converter module can be powered by any 3.7V LiIon/LiPoly battery, and convert the battery output to 5.2V DC for running your 5V projects.
  LIDAR-Lite: PulsedLight LIDAR-Lite Sensor
  Adafruit RFM9x LoRa Radio: Sending data over long distances is like magic, and now you can be a magician with this range of powerful and easy-to-use radio modules. Sure, sometimes you want to talk to a computer (a good time to use WiFi) or perhaps communicate with a Phone (choose Bluetooth Low Energy!) but what if you want to send data very far? Most WiFi, Bluetooth, Zigbee and other wireless chipsets use 2.4GHz, which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
  TXB0104 4-channel Bi-Directional Level Shifter: Because the Arduino (and Basic Stamp) are 5V devices, and most modern sensors, displays, flash cards and modes are 3.3V-only, many makers find that they need to perform level shifting/conversion to protect the 3.3V device from 5V. Although one can use resistors to make a divider, for high speed transfers, the resistors can add a lot of slew and cause havoc that is tough to debug. For that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
